// Logisim project Logisim nsi exo 3.circ as structural Verilog: 3 circuits, main circuit main
module main (
  input  A1,
  input  A2,
  input  A3,
  input  B1,
  input  B2,
  input  B3,
  output out_7
);

  wire demi_add_1_c;

  demi_add demi_add_1 (.a(A1), .b(B1), .c(demi_add_1_c), .s(out_7));
  add add_1 ();  // open: A, B, C1, C, S
endmodule

module demi_add (
  input  a,
  input  b,
  output c,
  output s
);

  wire and_2_out, and_3_out, not_1_out, not_2_out;

  and and_1 (c, a, b);
  not not_1 (not_1_out, a);
  not not_2 (not_2_out, b);
  and and_2 (and_2_out, not_1_out, b);
  and and_3 (and_3_out, a, not_2_out);
  or or_1 (s, and_2_out, and_3_out);
endmodule

module add (
  input  A,
  input  B,
  input  C1,
  output C,
  output S
);

  wire and_1_out, and_2_out, and_3_out, and_4_out, and_5_out, and_6_out, and_7_out, not_1_out, not_2_out,
       not_3_out, not_4_out, not_5_out, not_6_out;

  not not_1 (not_1_out, A);
  not not_2 (not_2_out, B);
  not not_3 (not_3_out, A);
  not not_4 (not_4_out, C1);
  not not_5 (not_5_out, B);
  not not_6 (not_6_out, C1);
  and and_1 (and_1_out, B, C1);
  and and_2 (and_2_out, A, C1);
  or or_1 (C, and_1_out, and_2_out, and_3_out);
  and and_3 (and_3_out, A, B);
  and and_4 (and_4_out, not_1_out, not_2_out, C1);
  and and_5 (and_5_out, not_3_out, B, not_4_out);
  and and_6 (and_6_out, A, not_5_out, not_6_out);
  and and_7 (and_7_out, A, B, C1);
  or or_2 (S, and_4_out, and_5_out, and_6_out, and_7_out);
endmodule
