// Logisim project Logisim nsi exo.circ as structural Verilog: 1 circuit, main circuit main
// a
module main (
  input  a,
  input  b,
  input  c,
  output out_4,
  output out_5,
  output out_6,
  output out_7,
  output out_8,
  output out_9
);

  wire and_2_out, not_2_out, not_3_out, not_4_out, not_5_out, or_3_out, or_4_out;

  not not_1 (out_4, a);
  not not_2 (not_2_out, a);
  not not_3 (not_3_out, b);
  not not_4 (not_4_out, c);
  or or_1 (out_5, a, b);
  and \and  (out_6, a, b);
  not not_5 (not_5_out, c);
  or or_2 (out_7, not_2_out, not_3_out);
  or or_3 (or_3_out, a, b);
  and and_2 (and_2_out, b, c);
  or or_4 (or_4_out, b, not_4_out);
  and and_3 (out_9, not_5_out, or_4_out);
  or or_5 (out_8, or_3_out, and_2_out);
endmodule
